# Fritzing sketch Adafruit_16_Channel_Servo_Driver_Zero (saved by Fritzing 0.9.3b)

parts:
  Raspberry_Pi_1 = Raspberry Pi 3 [part_number=RPI-3-V1.2]
  Part1 = 16-Channel 12-bit PWM Servo Driver - I2C [part_number=815]
  JACK1 = 2.1mm Barrel Jack with Terminal Block  # not connected
  J1 = Basic Servo
  J2 = Basic Servo

nets:
  3V3: Raspberry_Pi_1.3v3, Raspberry_Pi_1.3V3, Part1.VCC
  N1: Raspberry_Pi_1.GPIO2, Part1.SDA
  N2: Raspberry_Pi_1.GPIO3, Part1.SCL
  GND: Raspberry_Pi_1.GND, Part1.GND, J1.gnd, J2.gnd
  N3: Part1.PWM0, J1.pulse
  VCC: Part1.5.0V, J1.vcc, J2.vcc
  N4: Part1.PWM15, J2.pulse

notes:
  5v power supply
  Motor1
  Motor2

custom parts:
  16-Channel 12-bit PWM Servo Driver - I2C: You want to make a cool robot, maybe a hexapod walker, or maybe just a piece of art with a lot of moving parts. Or maybe you want to drive a lot of LEDs with precise PWM output. Using only two pins, control 16 free-running PWM outputs! You can even chain up 62 breakouts to control up to 992 PWM outputs.
