# Fritzing sketch Easy_Driver_Four_Stepper_Motors (saved by Fritzing 0.9.3b)

parts:
  Part1 = EasyDriver_v44
  M3 = Stepper Motor - Bipolar
  JACK1 = 2.1mm Barrel Jack with Terminal Block
  MCU1 = Raspberry Pi Zero
  Part2 = EasyDriver_v44
  M4 = Stepper Motor - Bipolar
  JACK2 = 2.1mm Barrel Jack with Terminal Block
  Part3 = EasyDriver_v44
  M5 = Stepper Motor - Bipolar
  JACK3 = 2.1mm Barrel Jack with Terminal Block
  Part4 = EasyDriver_v44
  M6 = Stepper Motor - Bipolar
  JACK4 = 2.1mm Barrel Jack with Terminal Block

nets:
  GND: Part1.GND, JACK1.NEG, MCU1.pin_6, MCU1.pin_9, MCU1.pin_25, MCU1.pin_39, Part2.GND, JACK2.NEG, Part3.GND, JACK3.NEG, Part4.GND, JACK4.NEG
  N1: Part1.V+, JACK1.POS
  N2: Part1.STEP, MCU1.pin_12
  N3: Part1.DIR, MCU1.pin_16
  N4: Part1.OUT2A, M3.A
  N5: Part1.OUT2B, M3.D
  N6: Part1.OUT1A, M3.B
  N7: Part1.OUT1B, M3.C
  N8: Part1.MS1, MCU1.pin_18
  N9: Part1.ENABLE, MCU1.pin_32
  N10: Part1.MS2, MCU1.pin_22
  N11: MCU1.pin_3, Part4.MS2
  N12: MCU1.pin_5, Part4.MS1
  N13: MCU1.pin_7, Part4.DIR
  N14: MCU1.pin_8, Part4.ENABLE
  N15: MCU1.pin_11, Part4.STEP
  N16: MCU1.pin_13, Part3.ENABLE
  N17: MCU1.pin_15, Part3.MS2
  N18: MCU1.pin_29, Part3.MS1
  N19: MCU1.pin_31, Part3.DIR
  N20: MCU1.pin_33, Part3.STEP
  N21: MCU1.pin_35, Part2.ENABLE
  N22: MCU1.pin_36, Part2.STEP
  N23: MCU1.pin_37, Part2.MS2
  N24: MCU1.pin_38, Part2.DIR
  N25: MCU1.pin_40, Part2.MS1
  N26: Part2.V+, JACK2.POS
  N27: Part2.OUT2A, M4.A
  N28: Part2.OUT2B, M4.D
  N29: Part2.OUT1A, M4.B
  N30: Part2.OUT1B, M4.C
  N31: Part3.V+, JACK3.POS
  N32: Part3.OUT2A, M5.A
  N33: Part3.OUT2B, M5.D
  N34: Part3.OUT1A, M5.B
  N35: Part3.OUT1B, M5.C
  N36: Part4.V+, JACK4.POS
  N37: Part4.OUT2A, M6.A
  N38: Part4.OUT2B, M6.D
  N39: Part4.OUT1A, M6.B
  N40: Part4.OUT1B, M6.C

notes:
  Jumber
  12V power Supply
  Motor1
  Motor2
  Motor3
  Motor4
