# Fritzing sketch Easy_Driver_Stepper_Motors (saved by Fritzing 0.9.3b)

parts:
  Part1 = EasyDriver_v44
  M1 = Stepper Motor - Bipolar  # not connected
  M2 = Stepper Motor - Bipolar  # not connected
  M3 = Stepper Motor - Bipolar
  M4 = Stepper Motor - Bipolar  # not connected
  Part2 = EasyDriver_v44  # not connected
  JACK1 = 2.1mm Barrel Jack with Terminal Block
  MCU1 = Raspberry Pi Zero

nets:
  N1: Part1.GND, JACK1.NEG, MCU1.pin_6, MCU1.pin_9
  N2: Part1.V+, JACK1.POS
  N3: Part1.STEP, MCU1.pin_12
  N4: Part1.DIR, MCU1.pin_16
  N5: Part1.OUT2A, M3.A
  N6: Part1.OUT2B, M3.D
  N7: Part1.OUT1A, M3.B
  N8: Part1.OUT1B, M3.C
  N9: Part1.MS1, MCU1.pin_18
  N10: Part1.ENABLE, MCU1.pin_24
  N11: Part1.MS2, MCU1.pin_22

notes:
  Jumber
  12V power Supply
